# Fritzing sketch MrBaladuino_1206_reworked (saved by Fritzing 0.8.5b)
circuit board: 5.2291cm x 2.08595cm
breadboards: 1

parts:
  J1 = female pin header, 1 pin [form="♀ (female)"]
  ATtiny85 = ATTINY45 [package=dip]
  LED2 = smd LED [color="Blue (430nm)" package="1206 [SMD]"]
  D2 = Rectifier Diode [package="Melf DO-213 AA [SMD]"]
  X1 = USB Connectors [package=usb-microb]
  D1 = Rectifier Diode [package="Melf DO-213 AA [SMD]"]
  R1 = Resistor [tolerance=±1% resistance=68 package="1206 [SMD]"]
  R2 = Resistor [tolerance=±1% resistance=68 package="1206 [SMD]"]
  R3 = Resistor [tolerance=±1% resistance=1.5k package="1206 [SMD]"]
  R5 = Resistor [tolerance=±1% resistance=1.5k package="1206 [SMD]"]
  LED1 = smd LED [color="Red (633nm)" package="1206 [SMD]"]
  C1 = Ceramic Capacitor [capacitance=100nF voltage=50V package="1206 [SMD, multilayer]"]
  R4 = Resistor [tolerance=±1% resistance=47k package="1206 [SMD]"]
  R6 = Resistor [tolerance=±1% resistance=1.5k package="1206 [SMD]"]
  USB = male pin header, 4 pins [form="♂ (male)"]

nets:
  N1: J1.pin1, R4.Pin_0
  N2: ATtiny85.PB5(NRES), R2.Pin_1
  N3: ATtiny85.PB3(ADC3), R1.Pin_1
  N4: ATtiny85.PB4(ADC2), R4.Pin_1
  GND: ATtiny85.GND, LED2.cathode, D2.anode, X1.GND, D1.anode, LED1.cathode, C1.0, USB.pin1
  N5: ATtiny85.PB0(MOSI), R6.Pin_1
  N6: ATtiny85.VCC, X1.VBUS, R3.Pin_1, R5.Pin_1, C1.1, USB.pin4
  N7: LED2.anode, R6.Pin_0
  N8: D2.cathode, X1.D-, R2.Pin_0, R3.Pin_0, USB.pin3
  N9: X1.D+, D1.cathode, R1.Pin_0, USB.pin2
  N10: R5.Pin_0, LED1.anode
