# Fritzing sketch MrBaladuinoDIL (saved by Fritzing 0.8.5b)
circuit board: 6.68051cm x 4.85042cm
breadboards: 1

parts:
  U2 = attiny85 [package=dip]
  R2 = Resistor [tolerance=±5% resistance=68 package=THT]
  R3 = Resistor [tolerance=±5% resistance=68 package=THT]
  R4 = Resistor [tolerance=±5% resistance=1.5k package=THT]
  CONN1 = USB connector [package=THT]
  D2 = Zener Diode [part_number=1N4732A breakdown_voltage=3.6V package="300 mil [THT]"]
  R6 = Resistor [tolerance=±5% resistance=1.5k package=THT]
  R5 = Resistor [tolerance=±5% resistance=1.5k package=THT]
  J1 = female pin header, 1 pin [form="♀ (female)"]
  C1 = Ceramic Capacitor [capacitance=100nF voltage=50V package="200 mil [THT, multilayer]"]
  D1 = Zener Diode [part_number=1N4732A breakdown_voltage=3.6V package="300 mil [THT]"]
  LED1 = LED - 3mm [color="Red (633nm)" package="3 mm [THT]"]
  LED2 = LED - 3mm [color="Blue (430nm)" package="3 mm [THT]"]

nets:
  N1: U2.Pin_1, R2.Pin_1
  N2: U2.Pin_2, R3.Pin_1
  N3: U2.Pin_3, J1.pin1
  N4: U2.Pin_4, CONN1.GND, CONN1.chassis5, CONN1.chassis6, D2.anode, C1.0, D1.anode, LED1.cathode
  N5: U2.Pin_5, R6.Pin_1
  N6: U2.Pin_8, R4.Pin_1, CONN1.5V, R5.Pin_1, C1.1
  N7: R2.Pin_0, R4.Pin_0, CONN1.d-, D2.cathode
  N8: R3.Pin_0, CONN1.d+, D1.cathode
  N9: R6.Pin_0, LED2.anode
  N10: R5.Pin_0, LED1.anode
